# Fritzing sketch HAPTIC_GLOVE_CIRCUIT (saved by Fritzing 0.9.10b)

parts:
  R1 = Basic Flex Resistor
  R2 = Basic Flex Resistor
  R3 = Basic Flex Resistor
  R4 = Basic Flex Resistor
  R5 = Basic Flex Resistor
  J1 = Basic Servo  # not connected
  J6 = Basic Servo  # not connected
  U1 = Voltage Regulator [package=v-reg_dpack]
  Power_plug1 = Power plug
  J3 = Basic Servo
  J4 = Basic Servo  # not connected
  J7 = Basic Servo  # not connected
  Nano1 = Arduino Nano v2.3
  Mod1 = Amica NodeMCU DEVKIT 1.0

nets:
  N1: R1.Pin_2, Nano1.D2, Mod1.pin_20
  N2: R2.Pin_2, Nano1.D3, Mod1.pin_21
  N3: R3.Pin_2, Nano1.D4, Mod1.pin_22
  N4: R4.Pin_2, Nano1.D5, Mod1.pin_23
  N5: R5.pin_1, Nano1.D6, Mod1.pin_24
  N6: U1.IN, Power_plug1.GND
  N7: J3.gnd, Nano1.D12, Mod1.pin_30
  N8: Nano1.D9, Mod1.pin_27

notes:
  Flex sensors
  Servo motors
  power adapter
  power supply
  ESP MCU (inbuilt bluetooth)
